# Fritzing sketch Untitled Sketch (saved by Fritzing 0.9.3b)
breadboards: 1

parts:
  U1 = ESP32S-HiLetgo [part_number=ESP32S-HiLetgo]
  7_Segment2 = 7 Segment Display
  R5 = Resistor [tolerance=±5% resistance=330 package="0603 [SMD]"]
  R6 = Resistor [tolerance=±5% resistance=330 package="0603 [SMD]"]
  R7 = Resistor [tolerance=±5% resistance=330 package="0603 [SMD]"]
  R8 = Resistor [tolerance=±5% resistance=330 package="0603 [SMD]"]
  Q2 = PNP-Transistor [package="TO92 [THT]"]
  R9 = Resistor [tolerance=±5% resistance=330 package="0603 [SMD]"]
  R10 = Resistor [tolerance=±5% resistance=330 package="0603 [SMD]"]
  R11 = Resistor [tolerance=±5% resistance=330 package="0603 [SMD]"]
  R12 = Resistor [tolerance=±5% resistance=330 package="0603 [SMD]"]
  R13 = Resistor [tolerance=±5% resistance=1k package="0603 [SMD]"]
  7_Segment3 = 7 Segment Display
  Q3 = PNP-Transistor [package="TO92 [THT]"]
  R14 = Resistor [tolerance=±5% resistance=1k package="0603 [SMD]"]

nets:
  N1: U1.GPIO36, R9.Pin_1
  N2: U1.GPIO39, R10.Pin_1
  N3: U1.GPIO34, R11.Pin_1
  N4: U1.GPIO35, R12.Pin_1
  N5: U1.GPIO25, R13.Pin_0
  N6: U1.GPIO14, R14.Pin_0
  N7: U1.GPIO21, R5.Pin_1
  N8: U1.GPIO3, R6.Pin_1
  N9: U1.GPIO1, R7.Pin_1
  N10: U1.GPIO22, R8.Pin_1
  N11: 7_Segment2.Segment_E, R10.Pin_0, 7_Segment3.Segment_E
  N12: 7_Segment2.Segment_D, R11.Pin_0, 7_Segment3.Segment_D
  N13: 7_Segment2.common_cathode, Q2.C, 7_Segment3.Segment_C
  N14: 7_Segment2.Segment_C, R12.Pin_0
  N15: 7_Segment2.Segment_DP, R9.Pin_0, 7_Segment3.Segment_DP
  N16: 7_Segment2.Segment_B, R8.Pin_0, 7_Segment3.Segment_B
  N17: 7_Segment2.Segment_A, R5.Pin_0, 7_Segment3.Segment_A
  N18: 7_Segment2.Segment_F, R6.Pin_0, 7_Segment3.Segment_F
  N19: 7_Segment2.Segment_G, R7.Pin_0, 7_Segment3.Segment_G
  N20: Q2.E, Q3.E
  N21: Q2.B, R13.Pin_1
  N22: 7_Segment3.common_cathode, Q3.C
  N23: Q3.B, R14.Pin_1

custom parts:
  ESP32S-HiLetgo: HiLetgo ESP-WROOM-32 ESP32 ESP-32S Development Board 2.4GHz Dual-Mode WiFi + Bluetooth Dual Cores Microcontroller The ESP32 integrated with Antenna switches, RF Balun, power amplifiers, low-noise amplifiers, filters, and management modules, and the entire solution occupies the least area of PCB. 2.4 GHz Wi-Fi plus Bluetooth dual-mode chip, with TSMC Ultra-low power consumption 40nm technology,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
